# Fritzing sketch ir_keyboard (saved by Fritzing 0.9.2b)
breadboards: 1

parts:
  Digispark1 = Digispark
  IR1 = TSOP312.., 314.. [package=THT]
  R1 = Resistor [tolerance=±5% resistance=10k package="1206 [SMD]"]

nets:
  N1: Digispark1.VCC, IR1.Vs, R1.Pin_0
  GND: Digispark1.GND, IR1.GND
  N2: Digispark1.P2, IR1.Data, R1.Pin_1

custom parts:
  Digispark: The Digispark is an Attiny85 based microcontroller development board similar to the Arduino line, only cheaper, smaller, and a bit less powerful. With a whole host of shields to extend its functionality and the ability to use the familiar Arduino IDE the Digispark is a great way to jump into electronics, or perfect for when an Arduino is too big or too much.
